# Fritzing sketch schema (saved by Fritzing 0.9.3b)
breadboards: 1

parts:
  MKRFox1 = Arduino MKR Fox 1200
  R1 = Resistor [tolerance=±5% resistance=10k package=THT]
  R2 = Resistor [tolerance=±5% resistance=10k package=THT]
  Composant1 = Triple Axis Accelerometer Breakout - ADXL345
  LED1 = LED - 5mm [color="Yellow (595nm)" package="5 mm [THT]"]
  LED2 = LED - 5mm [color="Red (633nm)" package="5 mm [THT]"]

nets:
  GND: MKRFox1.GND, Composant1.GND, LED1.anode, LED2.anode
  N1: MKRFox1.D4_PWM, LED1.cathode
  N2: MKRFox1.D5_PWM, LED2.cathode
  VCC: MKRFox1.VCC, R1.Pin_0, R2.Pin_0, Composant1.VCC, Composant1.CS, Composant1.INT1
  N3: MKRFox1.12/SCL, R1.Pin_1, Composant1.SCL
  N4: MKRFox1.11/SDA, R2.Pin_1, Composant1.SDA

notes:
  GP2Y0E03
